// Logisim project MemoryWalker (1).circ as structural Verilog: 1 circuit, main circuit main
module main (
);

  wire clock_1_out, clock_2_out, clock_3_out, undriven;
  wire [3:0] register_1_q_2;
  wire [7:0] random_1_out;
  wire [11:0] register_1_q;
  wire [15:0] adder_1_out;

  Clock clock_1 (.out(clock_1_out));
  Hex_Digit_Display hex_digit_display_1 (.value(register_1_q_2));  // open: dp
  Register #(.width(16)) register_1 (
    .D(adder_1_out), .en(1'b1), .Q({register_1_q_2, register_1_q}), .clk(clock_1_out), .clr(1'b0));
  Hex_Digit_Display hex_digit_display_2 (.value(register_1_q[11:8]));  // open: dp
  Adder #(.width(16)) adder_1 (.a({register_1_q_2, register_1_q}), .b(16'h1), .out(adder_1_out));  // open: cin, cout
  Hex_Digit_Display hex_digit_display_3 (.value(register_1_q[7:4]));  // open: dp
  Clock clock_2 (.out(clock_2_out));
  Hex_Digit_Display hex_digit_display_4 (.value(register_1_q[3:0]));  // open: dp
  Random random_1 (.clk(clock_2_out), .next(1'b1), .out(random_1_out), .clr(1'b0));
  Clock clock_3 (.out(clock_3_out));
  RAM #(.addrWidth(16), .bus("separate")) ram_1 (
    .addr({register_1_q_2, register_1_q}), .din(random_1_out), .str(undriven), .clk(clock_3_out));  // open: data, sel, ld, clr
endmodule
